# Fritzing sketch liikennevalot (saved by Fritzing 0.9.3b)
breadboards: 1

parts:
  Raspberry_Pi_1 = Raspberry Pi 3 [part_number=RPI-3-V1.2]
  LED4 = LED - 5mm [color="Red (633nm)" package="5 mm [THT]"]
  LED5 = LED - 5mm [color="Green (570nm)" package="5 mm [THT]"]
  R4 = Resistor [tolerance=±5% resistance=56 package=THT]
  R5 = Resistor [tolerance=±5% resistance=56 package=THT]
  S1 = Pushbutton [package="[THT]"]
  R6 = Resistor [tolerance=±5% resistance=10k package=THT]
  R3 = Resistor [tolerance=±5% resistance=56 package=THT]
  R1 = Resistor [tolerance=±5% resistance=56 package=THT]
  R2 = Resistor [tolerance=±5% resistance=56 package=THT]
  LED6 = LED - 5mm [color="Red (633nm)" package="5 mm [THT]"]
  LED7 = LED - 5mm [color="Green (570nm)" package="5 mm [THT]"]
  LED8 = LED - 5mm [color="Yellow (592nm)" package="5 mm [THT]"]
  D1 = Rectifier Diode [part_number=1N4001 package="300 mil [THT]"]
  D2 = Rectifier Diode [part_number=1N4001 package="300 mil [THT]"]
  J1 = Infrared Proximity Sensor

nets:
  N1: Raspberry_Pi_1.GIPO19, S1.Pin_3, S1.Pin_4, R6.Pin_1
  N2: Raspberry_Pi_1.GIPO20, R2.Pin_0, D1.cathode
  N3: Raspberry_Pi_1.GIPO16, R3.Pin_0
  N4: Raspberry_Pi_1.GIPO24, J1.Vout
  GND: Raspberry_Pi_1.GND, LED4.cathode, LED5.cathode, R6.Pin_0, LED6.cathode, LED7.cathode, LED8.cathode, J1.GND
  5V: Raspberry_Pi_1.5V, S1.Pin_1, S1.Pin_2, J1.Vcc
  N5: LED4.anode, R4.Pin_1
  N6: LED5.anode, R5.Pin_1
  N7: R4.Pin_0, D2.anode
  N8: R3.Pin_1, LED6.anode
  N9: R1.Pin_0, D2.cathode
  N10: R1.Pin_1, LED7.anode
  N11: R2.Pin_1, LED8.anode
